// Logisim project hw4.circ as structural Verilog
module RegisterFile (
  input  RegWriteEnable,
  input  [2:0] rd,
  input  [2:0] rs1,
  input  [15:0] WriteData,
  input  reset,
  input  [2:0] rs2,
  input  clk,
  output [15:0] rs1_data,
  output [15:0] rs2_data
);

  wire decoder_1_out0, reg1, reg2, reg3, reg4, reg5, reg6, reg7;
  wire [15:0] out_reg1, out_reg2, out_reg3, out_reg4, out_reg5, out_reg6, out_reg7;

  Decoder #(.select(3)) decoder_1 (
    .out0(decoder_1_out0), .out1(reg1), .out2(reg2), .out3(reg3), .out4(reg4), .out5(reg5), .out6(reg6),
    .out7(reg7), .sel(rd), .en(RegWriteEnable));
  Reg reg_1 (.data_in(WriteData), .clk(clk), .write_enable(reg1), .reset(reset), .data_out(out_reg1));
  Reg reg_2 (.data_in(WriteData), .clk(clk), .write_enable(reg2), .reset(reset), .data_out(out_reg2));
  Reg reg_3 (.data_in(WriteData), .clk(clk), .write_enable(reg3), .reset(reset), .data_out(out_reg3));
  Reg reg_4 (.data_in(WriteData), .clk(clk), .write_enable(reg4), .reset(reset), .data_out(out_reg4));
  Reg reg_5 (.data_in(WriteData), .clk(clk), .write_enable(reg5), .reset(reset), .data_out(out_reg5));
  Reg reg_6 (.data_in(WriteData), .clk(clk), .write_enable(reg6), .reset(reset), .data_out(out_reg6));
  Reg reg_7 (.data_in(WriteData), .clk(clk), .write_enable(reg7), .reset(reset), .data_out(out_reg7));
  Multiplexer #(.select(3), .width(16), .enable("false")) multiplexer_1 (
    .in0({16{1'b0}}), .in1(out_reg1), .in2(out_reg2), .in3(out_reg3), .in4(out_reg4), .in5(out_reg5),
    .in6(out_reg6), .in7(out_reg7), .out(rs1_data), .sel(rs1));
  Multiplexer #(.select(3), .width(16), .enable("false")) multiplexer_2 (
    .in0({16{1'b0}}), .in1(out_reg1), .in2(out_reg2), .in3(out_reg3), .in4(out_reg4), .in5(out_reg5),
    .in6(out_reg6), .in7(out_reg7), .out(rs2_data), .sel(rs2));

  // Other names for the same wires on the sheet: InputData[15:0] = WriteData; res = reset
endmodule

module Reg (
  input  [15:0] data_in,
  input  clk,
  input  write_enable,
  input  reset,
  output [15:0] data_out
);

  wire clkEnable;

  and and_1 (clkEnable, clk, write_enable);
  D_Flip_Flop d_ff_1 (.D(data_in[0]), .clk(clkEnable), .Q(data_out[0]), .reset(reset));  // open: Qn, preset
  D_Flip_Flop d_ff_2 (.D(data_in[1]), .clk(clkEnable), .Q(data_out[1]), .reset(reset));  // open: Qn, preset
  D_Flip_Flop d_ff_3 (.D(data_in[2]), .clk(clkEnable), .Q(data_out[2]), .reset(reset));  // open: Qn, preset
  D_Flip_Flop d_ff_4 (.D(data_in[3]), .clk(clkEnable), .Q(data_out[3]), .reset(reset));  // open: Qn, preset
  D_Flip_Flop d_ff_5 (.D(data_in[4]), .clk(clkEnable), .Q(data_out[4]), .reset(reset));  // open: Qn, preset
  D_Flip_Flop d_ff_6 (.D(data_in[5]), .clk(clkEnable), .Q(data_out[5]), .reset(reset));  // open: Qn, preset
  D_Flip_Flop d_ff_7 (.D(data_in[6]), .clk(clkEnable), .Q(data_out[6]), .reset(reset));  // open: Qn, preset
  D_Flip_Flop d_ff_8 (.D(data_in[7]), .clk(clkEnable), .Q(data_out[7]), .reset(reset));  // open: Qn, preset
  D_Flip_Flop d_ff_9 (.D(data_in[8]), .clk(clkEnable), .Q(data_out[8]), .reset(reset));  // open: Qn, preset
  D_Flip_Flop d_ff_10 (.D(data_in[9]), .clk(clkEnable), .Q(data_out[9]), .reset(reset));  // open: Qn, preset
  D_Flip_Flop d_ff_11 (.D(data_in[10]), .clk(clkEnable), .Q(data_out[10]), .reset(reset));  // open: Qn, preset
  D_Flip_Flop d_ff_12 (.D(data_in[11]), .clk(clkEnable), .Q(data_out[11]), .reset(reset));  // open: Qn, preset
  D_Flip_Flop d_ff_13 (.D(data_in[12]), .clk(clkEnable), .Q(data_out[12]), .reset(reset));  // open: Qn, preset
  D_Flip_Flop d_ff_14 (.D(data_in[13]), .clk(clkEnable), .Q(data_out[13]), .reset(reset));  // open: Qn, preset
  D_Flip_Flop d_ff_15 (.D(data_in[14]), .clk(clkEnable), .Q(data_out[14]), .reset(reset));  // open: Qn, preset
  D_Flip_Flop d_ff_16 (.D(data_in[15]), .clk(clkEnable), .Q(data_out[15]), .reset(reset));  // open: Qn, preset

  // Other names for the same wires on the sheet: in0 = data_in[0]; in1 = data_in[1]; in2 = data_in[2];
  //   in3 = data_in[3]; in4 = data_in[4]; in5 = data_in[5]; in6 = data_in[6]; in7 = data_in[7]; in8 = data_in[8];
  //   in9 = data_in[9]; in10 = data_in[10]; in11 = data_in[11]; in12 = data_in[12]; in13 = data_in[13];
  //   in14 = data_in[14]; in15 = data_in[15]; ot0 = data_out[0]; ot1 = data_out[1]; ot2 = data_out[2];
  //   ot3 = data_out[3]; ot4 = data_out[4]; ot5 = data_out[5]; ot6 = data_out[6]; ot7 = data_out[7];
  //   ot8 = data_out[8]; ot9 = data_out[9]; ot10 = data_out[10]; ot11 = data_out[11]; ot12 = data_out[12];
  //   ot13 = data_out[13]; ot14 = data_out[14]; ot15 = data_out[15]; res = reset
endmodule

module alu (
  input  [15:0] DataIn1,
  input  [15:0] DataIn2,
  input  [2:0] OpType,
  output [15:0] DataOut
);
endmodule
